# Fritzing sketch setup (saved by Fritzing 0.9.2b)
breadboards: 1

parts:
  R1 = Resistor [tolerance=±5% resistance=220 package=THT]
  Part1 = Arduino Uno (Rev3)
  J1 = Basic Servo
  IC1 = IC, DIP package, 8 pins [chip_label=IC]

nets:
  N1: R1.Pin_0, Part1.A0
  N2: R1.Pin_1, Part1.5V, IC1.pin2
  N3: Part1.D9_PWM, IC1.pin1
  N4: Part1.GND, IC1.pin3
  N5: J1.vcc, IC1.pin7
  N6: J1.pulse, IC1.pin8
